// Logisim project ALU.circ as structural Verilog
module Full_adder_alu (
  input  in_1,
  input  in_2,
  input  [15:0] in_3,
  input  [15:0] in_4,
  output [15:0] out_5,
  output out_6
);

  wire adder_1_cout, clock_1_out;
  wire [7:0] adder_1_out, adder_2_out;
  wire [15:0] bit_extender_1_out, xor_1_out;

  assign bit_extender_1_out = {{15{in_1}}, in_1};  // Bit_Extender bit_extender_1
  assign xor_1_out = bit_extender_1_out ^ {in_3[15:1], in_1};  // XOR_Gate xor_1, 16 bits wide
  Adder adder_1 (.a(xor_1_out[7:0]), .b(in_4[7:0]), .out(adder_1_out), .cin(in_1), .cout(adder_1_cout));
  Adder adder_2 (.a(xor_1_out[15:8]), .b(in_4[15:8]), .out(adder_2_out), .cin(adder_1_cout), .cout(out_6));
  Register #(.width(16)) register_1 (
    .D({adder_2_out, adder_1_out}), .en(in_2), .clk(clock_1_out), .Q(out_5));  // open: clr
  Clock clock_1 (.out(clock_1_out));

  assign in_3[0] = in_1;
endmodule

module Modulus_alu (
  input  [15:0] in_1,
  input  [15:0] in_2,
  output [15:0] out_3,
  output [15:0] out_4
);

  Divider #(.width(16)) divider_1 (.a(in_1), .b(in_2), .out(out_3), .rem(out_4));  // open: upper
endmodule

module and_alu (
  input  [15:0] in_1,
  input  [15:0] in_2,
  output [15:0] out_3
);

  assign out_3 = in_1 & in_2;  // AND_Gate and_1, 16 bits wide
endmodule

module not_alu (
  input  [15:0] in_1,
  output [15:0] out_2
);

  assign out_2 = ~in_1;  // NOT_Gate not_1, 16 bits wide
endmodule

module or_alu (
  input  [15:0] in_1,
  input  [15:0] in_2,
  output [15:0] out_3
);

  assign out_3 = in_1 | in_2;  // OR_Gate or_1, 16 bits wide
endmodule

module nand_alu (
  input  [15:0] in_1,
  input  [15:0] in_2,
  output [15:0] out_3
);

  assign out_3 = ~(in_1 & in_2);  // NAND_Gate nand_1, 16 bits wide
endmodule

module nor_alu (
  input  [15:0] in_1,
  input  [15:0] in_2,
  output [15:0] out_3
);

  assign out_3 = ~(in_1 | in_2);  // NOR_Gate nor_1, 16 bits wide
endmodule

module xor_alu (
  input  [15:0] in_1,
  input  [15:0] in_2,
  output [15:0] out_3
);

  assign out_3 = in_1 ^ in_2;  // XOR_Gate xor_1, 16 bits wide
endmodule

module xnor_alu (
  input  [15:0] in_1,
  input  [15:0] in_2,
  output [15:0] out_3
);

  assign out_3 = ~(in_1 ^ in_2);  // XNOR_Gate xnor_1, 16 bits wide
endmodule
